// Logisim project n16.circ as structural Verilog: 6 circuits, main circuit main
module main (
);

  wire ALU_C, ALU_N, ALU_Z, CLK, control_1_en_inst, control_1_en_mc_dec, control_1_mc_dec_0,
       control_1_mc_dec_1, control_1_out_23, control_1_out_25, control_1_out_26, control_1_out_27,
       control_1_out_28, control_1_out_29, control_1_out_30, control_1_out_31, control_1_out_32,
       control_1_out_33, EN_IR_0, EN_IR_1, EN_PC, EN_RAM, EN_RT, nCLK, PC_S_0, PC_S_1, RAM_R, SEL_ALU,
       SEL_RS, SEL_RT;
  wire [1:0] BUS_ALU_OP;
  wire [7:0] rom_1_data;
  wire [7:2] IR_0_q;
  wire [9:2] BUS_IMM10;
  wire [15:0] adder_1_out, adder_2_out, ALU_OUT, multiplexer_1_out, pc_imm_aligned_sign_extend_1_out,
       register_1_q, RS_DATA_OUT, RT_DATA_IN, RT_DATA_OUT;

  Clock clock_1 (.out(CLK));
  not not_1 (nCLK, CLK);
  pc_imm_aligned_sign_extend pc_imm_aligned_sign_extend_1 (
    .IN({BUS_IMM10, BUS_ALU_OP}), .OUT(pc_imm_aligned_sign_extend_1_out));
  Adder #(.width(16)) adder_1 (.a(register_1_q), .b(16'h1), .out(adder_1_out));  // open: cin, cout
  Adder #(.width(16)) adder_2 (
    .a(register_1_q), .b(pc_imm_aligned_sign_extend_1_out), .out(adder_2_out));  // open: cin, cout
  Multiplexer #(.select(2), .width(16), .enable("false")) multiplexer_1 (
    .in0(adder_1_out), .in1(adder_2_out), .in2(ALU_OUT), .out(multiplexer_1_out), .sel({PC_S_1, PC_S_0}));  // open: in3
  Register #(.width(16)) register_1 (.D(multiplexer_1_out), .en(EN_PC), .Q(register_1_q), .clk(nCLK));  // open: clr
  register_unit register_unit_1 (
    .BUS_RS(BUS_IMM10[9:6]), .SEL_RS(SEL_RS), .RT_DATA_IN(RT_DATA_IN), .RT_DATA_OUT(RT_DATA_OUT),
    .RS_DATA_OUT(RS_DATA_OUT), .EN_RT(EN_RT), .BUS_RT(BUS_IMM10[5:2]), .CLK(CLK), .SEL_RT(SEL_RT));
  ROM #(.addrWidth(16)) rom_1 (.addr(register_1_q), .data(rom_1_data), .sel(EN_RAM));
  Register IR_1 (.D(rom_1_data), .en(EN_IR_1), .Q({BUS_IMM10[7:2], BUS_ALU_OP}), .clk(CLK));  // open: clr
  Register IR_0 (.D(rom_1_data), .en(EN_IR_0), .Q({IR_0_q, BUS_IMM10[9:8]}), .clk(CLK));  // open: clr
  control control_1 (
    .CLK(CLK), .BUS_INST(rom_1_data[7:2]), .ALU_C(ALU_C), .ALU_Z(ALU_Z), .ALU_2(ALU_N),
    .EN_INST(control_1_en_inst), .EN_MC_DEC(control_1_en_mc_dec), .MC_DEC_0(control_1_mc_dec_0),
    .MC_DEC_1(control_1_mc_dec_1), .out_14(EN_RT), .out_15(SEL_RT), .EN_IR_0(SEL_RS), .EN_IR_1(EN_IR_0),
    .PC_S_0(EN_IR_1), .PC_S_1(PC_S_0), .EN_PC(PC_S_1), .EN_RAM(EN_PC), .RAM_R(EN_RAM),
    .out_23(control_1_out_23), .out_24(SEL_ALU), .out_25(control_1_out_25), .out_26(control_1_out_26),
    .out_27(control_1_out_27), .out_28(control_1_out_28), .out_29(control_1_out_29),
    .out_30(control_1_out_30), .out_31(control_1_out_31), .out_32(control_1_out_32), .out_33(control_1_out_33));  // open: IRQ_0, IRQ_1, IRQ_2, IRQ_3
  alu alu_1 (
    .R_S(RS_DATA_OUT), .R_T(RT_DATA_OUT), .ALU_OP(BUS_ALU_OP), .SEL_ALU(SEL_ALU), .ALU_OUT(ALU_OUT),
    .Z(ALU_Z), .C(ALU_C), .N(ALU_N));
  LED led_1 (.in(control_1_en_inst));
  LED led_2 (.in(control_1_en_mc_dec));
  LED led_3 (.in(control_1_mc_dec_0));
  LED led_4 (.in(control_1_mc_dec_1));
  LED led_5 (.in(EN_RT));
  LED led_6 (.in(SEL_RT));
  LED led_7 (.in(SEL_RS));
  LED led_8 (.in(EN_IR_0));
  LED led_9 (.in(EN_IR_1));
  LED led_10 (.in(PC_S_0));
  LED led_11 (.in(PC_S_1));
  LED led_12 (.in(EN_PC));
  LED led_13 (.in(EN_RAM));
  LED led_14 (.in(RAM_R));
  LED led_15 (.in(SEL_ALU));
  LED led_16 (.in(control_1_out_25));
  LED led_17 (.in(control_1_out_26));
  LED led_18 (.in(control_1_out_27));
  LED led_19 (.in(control_1_out_28));
  LED led_20 (.in(control_1_out_29));
  LED led_21 (.in(control_1_out_30));
  LED led_22 (.in(control_1_out_31));
  LED led_23 (.in(control_1_out_32));
  LED led_24 (.in(control_1_out_33));

  // Other names for the same wires on the sheet: BUS_IMM10[1:0] = BUS_ALU_OP; BUS_RT[3:0] = BUS_IMM10[5:2];
  //   BUS_RS[3:0] = BUS_IMM10[9:6]

  // Notes on the sheet:
  //   contents of rom_1 (hex, n*v repeats v):
  //   aa cd ef 91 aa
endmodule

module control (
  input  CLK,
  input  [5:0] BUS_INST,
  input  ALU_C,
  input  ALU_Z,
  input  ALU_2,
  input  IRQ_0,
  input  IRQ_1,
  input  IRQ_2,
  input  IRQ_3,
  output EN_INST,
  output EN_MC_DEC,
  output MC_DEC_0,
  output MC_DEC_1,
  output out_14,
  output out_15,
  output EN_IR_0,
  output EN_IR_1,
  output PC_S_0,
  output PC_S_1,
  output EN_PC,
  output EN_RAM,
  output RAM_R,
  output out_23,
  output out_24,
  output out_25,
  output out_26,
  output out_27,
  output out_28,
  output out_29,
  output out_30,
  output out_31,
  output out_32,
  output out_33
);

  wire and_1_out, and_2_out, multiplexer_1_out, nCLK, not_2_out, not_3_out;
  wire [2:0] rom_2_data;
  wire [7:0] BUS_INST_t, register_1_q;

  not not_1 (nCLK, CLK);
  assign BUS_INST_t = not_2_out ? {BUS_INST, 2'b00} : 8'bz;  // Controlled_Buffer controlled_buffer_1
  not not_2 (not_2_out, EN_MC_DEC);
  Multiplexer #(.select(2), .enable("false")) multiplexer_1 (
    .in0(1'b1), .in1(ALU_C), .in2(ALU_Z), .in3(ALU_2), .out(multiplexer_1_out), .sel({MC_DEC_1, MC_DEC_0}));
  LED led_1 (.in(CLK));
  Register register_1 (.D(BUS_INST_t), .en(EN_INST), .Q(register_1_q), .clk(nCLK));  // open: clr
  and and_1 (and_1_out, multiplexer_1_out, EN_MC_DEC);
  and and_2 (and_2_out, not_3_out, EN_MC_DEC);
  not not_3 (not_3_out, multiplexer_1_out);
  ROM rom_1 (
    .addr(register_1_q), .data({EN_IR_1, EN_IR_0, out_15, out_14, MC_DEC_1, MC_DEC_0, EN_MC_DEC, EN_INST}));  // open: sel
  ROM rom_2 (.addr(register_1_q), .data({out_25, out_24, out_23, RAM_R, EN_RAM, rom_2_data}));  // open: sel
  ROM rom_3 (
    .addr(register_1_q), .data({out_33, out_32, out_31, out_30, out_29, out_28, out_27, out_26}));  // open: sel
  ROM rom_4 (.addr(register_1_q), .data(BUS_INST_t), .sel(and_1_out));
  ROM rom_5 (.addr(register_1_q), .data(BUS_INST_t), .sel(and_2_out));
  D_Flip_Flop d_ff_1 (.clk(CLK), .D(rom_2_data[0]), .Q(PC_S_0));  // open: Qn, preset, en, reset
  D_Flip_Flop d_ff_2 (.clk(CLK), .D(rom_2_data[1]), .Q(PC_S_1));  // open: Qn, preset, en, reset
  D_Flip_Flop d_ff_3 (.clk(CLK), .D(rom_2_data[2]), .Q(EN_PC));  // open: Qn, preset, en, reset

  // Notes on the sheet:
  //   contents of rom_1 (hex, n*v repeats v):
  //   a3 23 53 73 93 83 162*0 83
  //   contents of rom_2 (hex, n*v repeats v):
  //   af ea 43 9c 12 f9 162*0 1c
  //   contents of rom_3 (hex, n*v repeats v):
  //   ab cd ef 39 19 f4 23 32
  //   contents of rom_4 (hex, n*v repeats v):
  //   1 2 3 4 5 7*0 a9 aa 154*0 a9
endmodule

module _3_state_register (
  input  [15:0] D,
  input  sel_s,
  input  en,
  input  clk,
  input  _0,
  input  sel_t,
  output [15:0] Q_S,
  output [15:0] Q_T
);

  wire [15:0] register_1_q;

  Register #(.width(16)) register_1 (.D(D), .en(en), .Q(register_1_q), .clk(clk), .clr(_0));
  assign Q_S = sel_s ? register_1_q : 16'bz;  // Controlled_Buffer controlled_buffer_1
  Pull_Resistor pull_resistor_1 (.node(sel_s));
  assign Q_T = sel_t ? register_1_q : 16'bz;  // Controlled_Buffer controlled_buffer_2
  Pull_Resistor pull_resistor_2 (.node(sel_t));
endmodule

module register_unit (
  input  [15:0] RT_DATA_IN,
  input  EN_RT,
  input  SEL_RT,
  input  [3:0] BUS_RT,
  input  [3:0] BUS_RS,
  input  CLK,
  input  SEL_RS,
  output [15:0] RT_DATA_OUT,
  output [15:0] RS_DATA_OUT
);

  wire decoder_1_out0, decoder_1_out1, decoder_1_out2, decoder_1_out3, decoder_1_out4, decoder_1_out5,
       decoder_1_out6, decoder_1_out7, decoder_1_out8, decoder_1_out9, decoder_1_out10, decoder_1_out11,
       decoder_1_out12, decoder_1_out13, decoder_1_out14, decoder_1_out15, decoder_2_out0, decoder_2_out1,
       decoder_2_out2, decoder_2_out3, decoder_2_out4, decoder_2_out5, decoder_2_out6, decoder_2_out7,
       decoder_2_out8, decoder_2_out9, decoder_2_out10, decoder_2_out11, decoder_2_out12, decoder_2_out13,
       decoder_2_out14, decoder_2_out15, decoder_3_out0, decoder_3_out1, decoder_3_out2, decoder_3_out3,
       decoder_3_out4, decoder_3_out5, decoder_3_out6, decoder_3_out7, decoder_3_out8, decoder_3_out9,
       decoder_3_out10, decoder_3_out11, decoder_3_out12, decoder_3_out13, decoder_3_out14, decoder_3_out15;

  Decoder #(.select(4)) decoder_1 (
    .out0(decoder_1_out0), .out1(decoder_1_out1), .out2(decoder_1_out2), .out3(decoder_1_out3),
    .out4(decoder_1_out4), .out5(decoder_1_out5), .out6(decoder_1_out6), .out7(decoder_1_out7),
    .out8(decoder_1_out8), .out9(decoder_1_out9), .out10(decoder_1_out10), .out11(decoder_1_out11),
    .out12(decoder_1_out12), .out13(decoder_1_out13), .out14(decoder_1_out14), .out15(decoder_1_out15),
    .sel(BUS_RT), .en(EN_RT));
  Decoder #(.select(4)) decoder_2 (
    .out0(decoder_2_out0), .out1(decoder_2_out1), .out2(decoder_2_out2), .out3(decoder_2_out3),
    .out4(decoder_2_out4), .out5(decoder_2_out5), .out6(decoder_2_out6), .out7(decoder_2_out7),
    .out8(decoder_2_out8), .out9(decoder_2_out9), .out10(decoder_2_out10), .out11(decoder_2_out11),
    .out12(decoder_2_out12), .out13(decoder_2_out13), .out14(decoder_2_out14), .out15(decoder_2_out15),
    .sel(BUS_RS), .en(SEL_RS));
  _3_state_register u_3_state_register_1 (
    .D(RT_DATA_IN), .en(decoder_1_out0), .clk(CLK), .sel_s(decoder_2_out0), .sel_t(decoder_3_out0),
    .Q_S(RS_DATA_OUT), .Q_T(RT_DATA_OUT));  // open: _0
  _3_state_register u_3_state_register_2 (
    .D(RT_DATA_IN), .en(decoder_1_out4), .clk(CLK), .sel_s(decoder_2_out4), .sel_t(decoder_3_out4),
    .Q_S(RS_DATA_OUT), .Q_T(RT_DATA_OUT));  // open: _0
  _3_state_register u_3_state_register_3 (
    .D(RT_DATA_IN), .en(decoder_1_out8), .clk(CLK), .sel_s(decoder_2_out8), .sel_t(decoder_3_out8),
    .Q_S(RS_DATA_OUT), .Q_T(RT_DATA_OUT));  // open: _0
  _3_state_register u_3_state_register_4 (
    .D(RT_DATA_IN), .en(decoder_1_out12), .clk(CLK), .sel_s(decoder_2_out12), .sel_t(decoder_3_out12),
    .Q_S(RS_DATA_OUT), .Q_T(RT_DATA_OUT));  // open: _0
  _3_state_register u_3_state_register_5 (
    .D(RT_DATA_IN), .en(decoder_1_out1), .clk(CLK), .sel_s(decoder_2_out1), .sel_t(decoder_3_out1),
    .Q_S(RS_DATA_OUT), .Q_T(RT_DATA_OUT));  // open: _0
  _3_state_register u_3_state_register_6 (
    .D(RT_DATA_IN), .en(decoder_1_out5), .clk(CLK), .sel_s(decoder_2_out5), .sel_t(decoder_3_out5),
    .Q_S(RS_DATA_OUT), .Q_T(RT_DATA_OUT));  // open: _0
  _3_state_register u_3_state_register_7 (
    .D(RT_DATA_IN), .en(decoder_1_out9), .clk(CLK), .sel_s(decoder_2_out9), .sel_t(decoder_3_out9),
    .Q_S(RS_DATA_OUT), .Q_T(RT_DATA_OUT));  // open: _0
  _3_state_register u_3_state_register_8 (
    .D(RT_DATA_IN), .en(decoder_1_out13), .clk(CLK), .sel_s(decoder_2_out13), .sel_t(decoder_3_out13),
    .Q_S(RS_DATA_OUT), .Q_T(RT_DATA_OUT));  // open: _0
  _3_state_register u_3_state_register_9 (
    .D(RT_DATA_IN), .en(decoder_1_out2), .clk(CLK), .sel_s(decoder_2_out2), .sel_t(decoder_3_out2),
    .Q_S(RS_DATA_OUT), .Q_T(RT_DATA_OUT));  // open: _0
  _3_state_register u_3_state_register_10 (
    .D(RT_DATA_IN), .en(decoder_1_out6), .clk(CLK), .sel_s(decoder_2_out6), .sel_t(decoder_3_out6),
    .Q_S(RS_DATA_OUT), .Q_T(RT_DATA_OUT));  // open: _0
  _3_state_register u_3_state_register_11 (
    .D(RT_DATA_IN), .en(decoder_1_out10), .clk(CLK), .sel_s(decoder_2_out10), .sel_t(decoder_3_out10),
    .Q_S(RS_DATA_OUT), .Q_T(RT_DATA_OUT));  // open: _0
  _3_state_register u_3_state_register_12 (
    .D(RT_DATA_IN), .en(decoder_1_out14), .clk(CLK), .sel_s(decoder_2_out14), .sel_t(decoder_3_out14),
    .Q_S(RS_DATA_OUT), .Q_T(RT_DATA_OUT));  // open: _0
  _3_state_register u_3_state_register_13 (
    .D(RT_DATA_IN), .en(decoder_1_out3), .clk(CLK), .sel_s(decoder_2_out3), .sel_t(decoder_3_out3),
    .Q_S(RS_DATA_OUT), .Q_T(RT_DATA_OUT));  // open: _0
  _3_state_register u_3_state_register_14 (
    .D(RT_DATA_IN), .en(decoder_1_out7), .clk(CLK), .sel_s(decoder_2_out7), .sel_t(decoder_3_out7),
    .Q_S(RS_DATA_OUT), .Q_T(RT_DATA_OUT));  // open: _0
  _3_state_register u_3_state_register_15 (
    .D(RT_DATA_IN), .en(decoder_1_out11), .clk(CLK), .sel_s(decoder_2_out11), .sel_t(decoder_3_out11),
    .Q_S(RS_DATA_OUT), .Q_T(RT_DATA_OUT));  // open: _0
  _3_state_register u_3_state_register_16 (
    .D(RT_DATA_IN), .en(decoder_1_out15), .clk(CLK), .sel_s(decoder_2_out15), .sel_t(decoder_3_out15),
    .Q_S(RS_DATA_OUT), .Q_T(RT_DATA_OUT));  // open: _0
  Decoder #(.select(4)) decoder_3 (
    .out0(decoder_3_out0), .out1(decoder_3_out1), .out2(decoder_3_out2), .out3(decoder_3_out3),
    .out4(decoder_3_out4), .out5(decoder_3_out5), .out6(decoder_3_out6), .out7(decoder_3_out7),
    .out8(decoder_3_out8), .out9(decoder_3_out9), .out10(decoder_3_out10), .out11(decoder_3_out11),
    .out12(decoder_3_out12), .out13(decoder_3_out13), .out14(decoder_3_out14), .out15(decoder_3_out15),
    .sel(BUS_RT), .en(SEL_RT));
endmodule

module alu (
  input  [15:0] R_S,
  input  [15:0] R_T,
  input  [1:0] ALU_OP,
  input  SEL_ALU,
  output [15:0] ALU_OUT,
  output Z,
  output C,
  output N
);

  wire [15:0] adder_1_out, multiplier_1_out, subtractor_1_out;

  Adder #(.width(16)) adder_1 (.a(R_S), .b(R_T), .out(adder_1_out));  // open: cin, cout
  Subtractor #(.width(16)) subtractor_1 (.a(R_S), .b(R_T), .out(subtractor_1_out));  // open: bin, bout
  Multiplier #(.width(16)) multiplier_1 (.a(R_S), .b(R_T), .out(multiplier_1_out));  // open: cin, cout
  Multiplexer #(.select(2), .width(16)) multiplexer_1 (
    .in0(R_S), .in1(adder_1_out), .in2(subtractor_1_out), .in3(multiplier_1_out), .out(ALU_OUT),
    .sel(ALU_OP), .en(SEL_ALU));
  Pull_Resistor pull_resistor_1 (.node(C));

  assign N = C;
  assign Z = C;
endmodule

module pc_imm_aligned_sign_extend (
  input  [9:0] IN,
  output [15:0] OUT
);


  assign OUT = {{6{IN[9]}}, IN[8:0], 1'b0};
endmodule
